// Logisim project BCD_TO_7.circ as structural Verilog: 1 circuit, main circuit main
module main (
  input  w,
  input  x,
  input  y,
  input  z,
  output a,
  output b,
  output c,
  output d,
  output e,
  output f,
  output g
);

  wire and_1_out, and_2_out, and_3_out, and_4_out, and_5_out, and_6_out, and_7_out, and_8_out, and_9_out,
       and_10_out, and_11_out, and_12_out, and_13_out, and_14_out, and_15_out, and_16_out, not_1_out,
       not_2_out, not_3_out;

  not not_1 (not_1_out, x);
  not not_2 (not_2_out, y);
  not not_3 (not_3_out, z);
  and and_1 (and_1_out, not_1_out, not_3_out);
  and and_2 (and_2_out, x, z);
  and and_3 (and_3_out, not_2_out, not_3_out);
  and and_4 (and_4_out, y, z);
  or or_1 (c, not_2_out, z, x);
  and and_5 (and_5_out, not_1_out, not_3_out);
  and and_6 (and_6_out, not_1_out, y);
  and and_7 (and_7_out, x, not_2_out, z);
  and and_8 (and_8_out, y, not_3_out);
  and and_9 (and_9_out, not_1_out, not_3_out);
  and and_10 (and_10_out, y, not_3_out);
  and and_11 (and_11_out, not_2_out, not_3_out);
  and and_12 (and_12_out, x, not_2_out);
  and and_13 (and_13_out, x, not_3_out);
  and and_14 (and_14_out, not_1_out, y);
  and and_15 (and_15_out, x, not_2_out);
  and and_16 (and_16_out, y, not_3_out);
  or or_2 (a, and_1_out, y, and_2_out, w);
  or or_3 (b, not_1_out, and_3_out, and_4_out);
  or or_4 (d, and_5_out, and_6_out, and_7_out, and_8_out, w);
  or or_5 (e, and_9_out, and_10_out);
  or or_6 (f, and_11_out, and_12_out, and_13_out, w);
  or or_7 (g, and_14_out, and_15_out, w, and_16_out);
  _7_Segment_Display u_7_segment_display_1 (.g(g), .f(f), .a(a), .b(b), .e(e), .d(d), .c(c));  // open: dp
endmodule
