// Logisim project BCD_TO_DECIMAL_DECODER.circ as structural Verilog: 1 circuit, main circuit main
module main (
  input  X,
  input  Y,
  input  Z,
  output A,
  output B,
  output C,
  output D,
  output E,
  output F,
  output G,
  output H
);

  wire not_1_out, not_2_out, not_3_out;

  not not_1 (not_1_out, X);
  not not_2 (not_2_out, Y);
  not not_3 (not_3_out, Z);
  and and_1 (A, not_1_out, not_2_out, not_3_out);
  and and_2 (B, not_1_out, not_2_out, Z);
  and and_3 (C, not_1_out, Y, not_3_out);
  and and_4 (D, not_1_out, Y, Z);
  and and_5 (E, X, not_2_out, not_3_out);
  and and_6 (F, X, not_2_out, Z);
  and and_7 (G, X, Y, not_3_out);
  and and_8 (H, X, Y, Z);
endmodule
