// Logisim project DEMULTIPLEXER_2_TO_4.circ as structural Verilog: 1 circuit, main circuit main
module main (
  input  E,
  input  A,
  input  B,
  output W,
  output X,
  output Y,
  output Z
);

  wire not_1_out, not_2_out;

  not not_1 (not_1_out, A);
  not not_2 (not_2_out, B);
  or or_1 (W, B, A);
  or or_2 (X, not_2_out, A);
  or or_3 (Y, not_1_out, B);
  or or_4 (Z, not_1_out, not_2_out);
endmodule
